# Fritzing sketch EagleTree_RPM_sensors (saved by Fritzing 0.8.7b)
breadboards: 1

parts:
  Composant1 = Arduino Uno (Rev3)
  R1 = Resistor [tolerance=±5% resistance=100k package=THT]
  D1 = Rectifier Diode [part_number=1N4001 package="300 mil [THT]"]  # not connected
  J1 = female pin header, 3 pins [form="♀ (female)"]
  J2 = female pin header, 3 pins [form="♀ (female)"]
  R2 = Resistor [tolerance=±5% resistance=10k package=THT]
  R3 = Resistor [tolerance=±5% resistance=100 package=THT]

nets:
  N1: Composant1.D10_PWM/SS, R1.Pin_0
  N2: Composant1.D11_PWM/MOSI, J1.pin1
  N3: Composant1.D5_PWM, Composant1.GND, R1.Pin_1, J1.pin3, J2.pin1, J2.pin2, R2.Pin_0, R3.Pin_1
  N4: Composant1.5V, J1.pin2, R2.Pin_1
  N5: J2.pin3, R3.Pin_0

notes:
  Smart Port
  EagleTree brushless sensor
  Volt. red. 100 Ω
  Pull-up 100kΩ
  EagleTree opticalsensor
  Brushless sensor: pull-up 1kΩ
  Optical sensor: pull-up 10kΩ
  Hall sensor: pull-up 1kΩ or 10kΩ
