# Fritzing sketch Smart_Port (saved by Fritzing 0.9.2b)
breadboards: 1

parts:
  Composant1 = Arduino Uno (Rev3)
  R1 = Resistor [tolerance=±5% resistance=100k package=THT]
  D1 = Rectifier Diode [part_number=1N4001 package="300 mil [THT]"]
  J1 = female pin header, 3 pins [form="♀ (female)"]

nets:
  N1: Composant1.D10_PWM/SS, D1.cathode
  N2: Composant1.D11_PWM/MOSI, R1.Pin_0, D1.anode, J1.pin1
  N3: Composant1.5V, J1.pin2
  N4: Composant1.GND, R1.Pin_1, J1.pin3

notes:
  Smart Port
